// Logisim project CO_Project.circ as structural Verilog: 26 circuits, main circuit main
module main (
  input  START,
  input  RESET,
  input  FGI,
  input  [7:0] in_4,
  input  in_5,
  input  in_6,
  input  in_7,
  input  in_8,
  input  in_9,
  input  in_10,
  input  in_11,
  input  in_12
);

  wire clock_1_out, controlunit_1_ac_ld, controlunit_1_ac_out, controlunit_1_add, controlunit_1_andd,
       controlunit_1_ar_inc, controlunit_1_ar_ld, controlunit_1_ar_out, controlunit_1_cla, controlunit_1_cle,
       controlunit_1_cma, controlunit_1_dr_inc, controlunit_1_dr_ld, controlunit_1_dr_out,
       controlunit_1_inpr_ld, controlunit_1_inpr_out, controlunit_1_ir_adder_out, controlunit_1_ir_ld,
       controlunit_1_mem_read, controlunit_1_mem_write, controlunit_1_out_34, controlunit_1_out_35,
       controlunit_1_out_36, controlunit_1_out_37, controlunit_1_out_38, controlunit_1_out_39,
       controlunit_1_out_40, controlunit_1_outr_ld, controlunit_1_pc_inc, controlunit_1_pc_ld,
       controlunit_1_pc_out, controlunit_1_stop, controlunit_1_z_r, dataunit_1_e, dataunit_1_ir_i,
       dataunit_1_z, outputs_1_out_2, outputs_1_out_3, outputs_1_out_4, outputs_1_out_5, outputs_1_out_6,
       outputs_1_out_7, outputs_1_out_8, outputs_1_out_9;
  wire [3:0] b_to_d_1_out_2, b_to_d_1_out_3, b_to_d_1_out_4, dataunit_1_ir_opcode;
  wire [7:0] dataunit_1_outr_q, inputs_1_out_10, outputs_1_out_10;

  LED led_1 (.in(controlunit_1_stop));
  Clock clock_1 (.out(clock_1_out));
  ControlUnit controlunit_1 (
    .E(dataunit_1_e), .IR_I(dataunit_1_ir_i), .Z(dataunit_1_z), .D_FGI(FGI), .OPCODE(dataunit_1_ir_opcode),
    .RESET(RESET), .in_7(clock_1_out), .D_S(START), .INPR_OUT(controlunit_1_inpr_out),
    .OUTR_LD(controlunit_1_outr_ld), .INPR_LD(controlunit_1_inpr_ld), .AR_LD(controlunit_1_ar_ld),
    .CLE(controlunit_1_cle), .CMA(controlunit_1_cma), .AR_INC(controlunit_1_ar_inc),
    .IR_ADDER_OUT(controlunit_1_ir_adder_out), .STOP(controlunit_1_stop), .out_34(controlunit_1_out_34),
    .out_35(controlunit_1_out_35), .out_36(controlunit_1_out_36), .out_37(controlunit_1_out_37),
    .out_38(controlunit_1_out_38), .out_39(controlunit_1_out_39), .out_40(controlunit_1_out_40),
    .Z_R(controlunit_1_z_r), .PC_INC(controlunit_1_pc_inc), .DR_LD(controlunit_1_dr_ld),
    .AC_LD(controlunit_1_ac_ld), .MEM_WRITE(controlunit_1_mem_write), .ANDD(controlunit_1_andd),
    .PC_OUT(controlunit_1_pc_out), .IR_LD(controlunit_1_ir_ld), .PC_LD(controlunit_1_pc_ld),
    .DR_INC(controlunit_1_dr_inc), .MEM_READ(controlunit_1_mem_read), .ADD(controlunit_1_add),
    .CLA(controlunit_1_cla), .DR_OUT(controlunit_1_dr_out), .AC_OUT(controlunit_1_ac_out),
    .AR_OUT(controlunit_1_ar_out));
  LED led_2 (.in(outputs_1_out_2));
  LED led_3 (.in(outputs_1_out_3));
  OUTPUTS outputs_1 (
    .in_1(dataunit_1_outr_q), .out_2(outputs_1_out_2), .out_3(outputs_1_out_3), .out_4(outputs_1_out_4),
    .out_5(outputs_1_out_5), .out_6(outputs_1_out_6), .out_7(outputs_1_out_7), .out_8(outputs_1_out_8),
    .out_9(outputs_1_out_9), .out_10(outputs_1_out_10));
  LED led_4 (.in(outputs_1_out_6));
  LED led_5 (.in(outputs_1_out_7));
  LED led_6 (.in(outputs_1_out_4));
  LED led_7 (.in(outputs_1_out_5));
  LED led_8 (.in(outputs_1_out_8));
  LED led_9 (.in(outputs_1_out_9));
  B_TO_D b_to_d_1 (.in_1(outputs_1_out_10), .out_2(b_to_d_1_out_2), .out_3(b_to_d_1_out_3), .out_4(b_to_d_1_out_4));
  DataUnit dataunit_1 (
    .AR_OUT(controlunit_1_ar_out), .E_R(controlunit_1_cle), .CLA(controlunit_1_cla), .CMA(controlunit_1_cma),
    .ANDD(controlunit_1_andd), .AR_INC(controlunit_1_ar_inc), .ADD(controlunit_1_add),
    .OUTR_R(controlunit_1_out_40), .OUTR_LD(controlunit_1_outr_ld), .INPR_R(controlunit_1_out_39),
    .INPR_OUT(controlunit_1_inpr_out), .AR_R(controlunit_1_out_35), .INPR_D(inputs_1_out_10),
    .INPR_LD(controlunit_1_inpr_ld), .PC_LD(controlunit_1_pc_ld), .PC_OUT(controlunit_1_pc_out),
    .PC_INC(controlunit_1_pc_inc), .PC_R(controlunit_1_out_38), .IR_LD(controlunit_1_ir_ld),
    .IR_R(controlunit_1_out_37), .IR_ADDER_OUT(controlunit_1_ir_adder_out), .AC_LD(controlunit_1_ac_ld),
    .AC_OUT(controlunit_1_ac_out), .AC_R(controlunit_1_out_36), .DR_LD(controlunit_1_dr_ld),
    .DR_OUT(controlunit_1_dr_out), .DR_INC(controlunit_1_dr_inc), .DR_R(controlunit_1_out_34),
    .MEM_WRITE(controlunit_1_mem_write), .AR_LD(controlunit_1_ar_ld), .CLK(clock_1_out),
    .MEM_READ(controlunit_1_mem_read), .Z_R(controlunit_1_z_r), .E(dataunit_1_e), .OUTR_Q(dataunit_1_outr_q),
    .IR_OPCODE(dataunit_1_ir_opcode), .IR_I(dataunit_1_ir_i), .Z(dataunit_1_z));
  INPUTS inputs_1 (
    .in_2(in_5), .in_3(in_6), .in_4(in_7), .in_5(in_8), .in_6(in_9), .in_7(in_10), .in_8(in_11),
    .in_9(in_12), .in_1(in_4), .out_10(inputs_1_out_10));
  Hex_Digit_Display hex_digit_display_1 (.value(b_to_d_1_out_2));  // open: dp
  Hex_Digit_Display hex_digit_display_2 (.value(b_to_d_1_out_3));  // open: dp
  Hex_Digit_Display hex_digit_display_3 (.value(b_to_d_1_out_4));  // open: dp
endmodule

module DataUnit (
  input  CLK,
  input  [7:0] INPR_D,
  input  AR_LD,
  input  AR_OUT,
  input  AR_INC,
  input  AR_R,
  input  PC_LD,
  input  PC_OUT,
  input  PC_INC,
  input  PC_R,
  input  IR_LD,
  input  IR_R,
  input  IR_ADDER_OUT,
  input  AC_LD,
  input  AC_OUT,
  input  AC_R,
  input  DR_LD,
  input  DR_OUT,
  input  DR_INC,
  input  DR_R,
  input  MEM_WRITE,
  input  MEM_READ,
  input  Z_R,
  input  E_R,
  input  CLA,
  input  CMA,
  input  ANDD,
  input  ADD,
  input  OUTR_R,
  input  OUTR_LD,
  input  INPR_R,
  input  INPR_OUT,
  input  INPR_LD,
  output [7:0] OUTR_Q,
  output [3:0] IR_OPCODE,
  output IR_I,
  output Z,
  output E
);

  wire ac_register_1_out_9, alu_1_e, alu_1_out_8, alu_1_out_8_2, alu_1_z, ar_register_1_out_10,
       dr_register_1_out_10, ir_register_1_out_9, memory_1_out_6, pc_register_1_out_9, undriven;
  wire [1:0] select_alu_1_s;
  wire [10:0] ar_register_1_q, data_bus_1_mem_a;
  wire [15:0] ac_register_1_q, ac_register_1_q_out, alu_1_o, ar_register_1_q_out, data_bus_1_a, data_bus_1_b,
       data_bus_1_out_23, data_bus_1_out_24, data_bus_1_out_25, data_bus_1_out_26, data_bus_1_out_27,
       data_bus_1_out_28, data_bus_1_out_29, dr_register_1_q, dr_register_1_q_out, inpr_register_1_q_out,
       ir_register_1_ir_addr, memory_1_q, pc_register_1_q_out;

  AR_REGISTER ar_register_1 (
    .AR_OUT(AR_OUT), .LD(AR_LD), .D_in(data_bus_1_out_28), .CLK(CLK), .RESET(AR_R), .INC(AR_INC),
    .out_10(ar_register_1_out_10), .Q_Out(ar_register_1_q_out), .Q(ar_register_1_q));  // open: CLR
  PC_REGISTER pc_register_1 (
    .PC_OUT(PC_OUT), .LD(PC_LD), .D_in(data_bus_1_out_25), .CLK(CLK), .RESET(PC_R), .INC(PC_INC),
    .out_9(pc_register_1_out_9), .Q_Out(pc_register_1_q_out));  // open: CLR
  IR_REGISTER ir_register_1 (
    .D_in(data_bus_1_out_24), .LD(IR_LD), .CLK(CLK), .RESET(IR_R),
    .out_9({IR_ADDER_OUT, ir_register_1_out_9}), .IR_I(IR_I), .IR_OPCODE(IR_OPCODE),
    .IR_ADDR(ir_register_1_ir_addr));
  AC_REGISTER ac_register_1 (
    .AC_OUT(AC_OUT), .CLK(CLK), .D_in(data_bus_1_out_26), .LD(AC_LD), .RESET(AC_R),
    .out_9(ac_register_1_out_9), .Q_OUT(ac_register_1_q_out), .Q(ac_register_1_q));  // open: CLR
  DR_REGISTER dr_register_1 (
    .LD(DR_LD), .D_in(data_bus_1_out_29), .CLK(CLK), .RESET(DR_R), .INC(DR_INC),
    .out_10({DR_OUT, dr_register_1_out_10}), .Q(dr_register_1_q), .Q_OUT(dr_register_1_q_out));  // open: CLR
  DATA_BUS data_bus_1 (
    .DR_Q(dr_register_1_q), .AR_OUT(ar_register_1_out_10), .ALU_OUT(alu_1_out_8), .AR_Q(ar_register_1_q),
    .AC_Q(ac_register_1_q), .in_4(inpr_register_1_q_out), .in_5(dr_register_1_q_out), .in_6(memory_1_q),
    .in_7(pc_register_1_q_out), .in_8(ir_register_1_ir_addr), .in_9(ac_register_1_q_out),
    .in_10(ar_register_1_q_out), .in_11(alu_1_o), .INPR_OUT(undriven), .DR_OUT(dr_register_1_out_10),
    .MEM_READ(memory_1_out_6), .PC_OUT(pc_register_1_out_9), .IR_ADDER_OUT(ir_register_1_out_9),
    .AC_OUT(ac_register_1_out_9), .B(data_bus_1_b), .out_27(data_bus_1_out_27), .out_23(data_bus_1_out_23),
    .out_28(data_bus_1_out_28), .out_29(data_bus_1_out_29), .MEM_A(data_bus_1_mem_a), .A(data_bus_1_a),
    .out_24(data_bus_1_out_24), .out_25(data_bus_1_out_25), .out_26(data_bus_1_out_26));
  INPR_REGISTER inpr_register_1 (
    .LD(INPR_LD), .D_in(INPR_D), .CLK(CLK), .RESET(INPR_R), .AR_OUT({INPR_OUT, undriven}),
    .Q_Out(inpr_register_1_q_out));
  OUTR_REGISTER outr_register_1 (.LD(OUTR_LD), .D_in(data_bus_1_out_27), .CLK(CLK), .RESET(OUTR_R), .Q_Out(OUTR_Q));
  ALU alu_1 (
    .B(data_bus_1_b), .A(data_bus_1_a), .out_8({alu_1_out_8_2, alu_1_out_8}), .S(select_alu_1_s),
    .E(alu_1_e), .Z(alu_1_z), .O(alu_1_o));
  FLAGS flags_1 (.E(alu_1_e), .Z(alu_1_z), .CLK(CLK), .in_2(E_R), .in_4(Z_R), .out_6(E), .out_7(Z));
  MEMORY memory_1 (
    .O_E(MEM_READ), .WE(MEM_WRITE), .CLK(CLK), .D(data_bus_1_out_23), .A(data_bus_1_mem_a),
    .out_6(memory_1_out_6), .Q(memory_1_q));
  SELECT_ALU select_alu_1 (.ADD(ADD), .ANDD(ANDD), .CMA(CMA), .CLA(CLA), .EN(alu_1_out_8_2), .S(select_alu_1_s));

  // Notes on the sheet:
  //   DATA UNIT
endmodule

module ControlUnit (
  input  [3:0] OPCODE,
  input  D_FGI,
  input  D_S,
  input  E,
  input  IR_I,
  input  RESET,
  input  in_7,
  input  Z,
  output Z_R,
  output PC_INC,
  output DR_LD,
  output AC_LD,
  output MEM_WRITE,
  output ANDD,
  output PC_OUT,
  output IR_LD,
  output PC_LD,
  output DR_INC,
  output MEM_READ,
  output ADD,
  output CLA,
  output DR_OUT,
  output AC_OUT,
  output AR_OUT,
  output INPR_OUT,
  output OUTR_LD,
  output INPR_LD,
  output AR_LD,
  output CLE,
  output CMA,
  output AR_INC,
  output IR_ADDER_OUT,
  output STOP,
  output out_34,
  output out_35,
  output out_36,
  output out_37,
  output out_38,
  output out_39,
  output out_40
);

  wire and_1_out, control_logic_1_fgi_clr, control_logic_1_fgo_clr, control_logic_1_s_clr,
       control_logic_1_sc_clr, flags_i_o_1_q_i, flags_i_o_1_q_o, instruction_decoder_1_d0,
       instruction_decoder_1_d1, instruction_decoder_1_d2, instruction_decoder_1_d3,
       instruction_decoder_1_d4, instruction_decoder_1_d5, instruction_decoder_1_d6,
       instruction_decoder_1_d7, instruction_decoder_1_d8, instruction_decoder_1_d9,
       instruction_decoder_1_d10, instruction_decoder_1_d11, instruction_decoder_1_d12,
       instruction_decoder_1_d13, instruction_decoder_1_d14, instruction_decoder_1_d15, s_flag_1_out_put,
       t_flip_flop_1_out_2, t_flip_flop_2_out_2, timing_decoder_1_t0, timing_decoder_1_t1,
       timing_decoder_1_t2, timing_decoder_1_t3, timing_decoder_1_t4, timing_decoder_1_t5,
       timing_decoder_1_t6, timing_decoder_1_t7, timing_decoder_1_t8, timing_decoder_1_t9,
       timing_decoder_1_t10, timing_decoder_1_t11, timing_decoder_1_t12, timing_decoder_1_t13,
       timing_decoder_1_t14, timing_decoder_1_t15;
  wire [3:0] sequence_counter_1_o_p;

  T_FLIP_FLOP t_flip_flop_1 (.CLK(in_7), .out_2(t_flip_flop_1_out_2));
  and and_1 (and_1_out, t_flip_flop_1_out_2, s_flag_1_out_put);
  Sequence_Counter sequence_counter_1 (.EN_INC(and_1_out), .CLK(in_7), .RESET(Z_R), .O_P(sequence_counter_1_o_p));
  S_FLAG s_flag_1 (.START(D_S), .CLK(in_7), .RESET(control_logic_1_s_clr), .OUT_PUT(s_flag_1_out_put));
  and and_2 (Z_R, t_flip_flop_2_out_2, control_logic_1_sc_clr);
  T_FLIP_FLOP t_flip_flop_2 (.CLK(in_7), .out_2(t_flip_flop_2_out_2));
  Timing_Decoder timing_decoder_1 (
    .SC(sequence_counter_1_o_p), .T0(timing_decoder_1_t0), .T15(timing_decoder_1_t15),
    .T1(timing_decoder_1_t1), .T14(timing_decoder_1_t14), .T2(timing_decoder_1_t2),
    .T13(timing_decoder_1_t13), .T3(timing_decoder_1_t3), .T12(timing_decoder_1_t12),
    .T4(timing_decoder_1_t4), .T11(timing_decoder_1_t11), .T5(timing_decoder_1_t5),
    .T10(timing_decoder_1_t10), .T6(timing_decoder_1_t6), .T9(timing_decoder_1_t9), .T7(timing_decoder_1_t7),
    .T8(timing_decoder_1_t8));
  Control_Logic control_logic_1 (
    .IR_I(IR_I), .FGO(flags_i_o_1_q_o), .FGI(flags_i_o_1_q_i), .D0(instruction_decoder_1_d0),
    .D1(instruction_decoder_1_d1), .D2(instruction_decoder_1_d2), .D3(instruction_decoder_1_d3),
    .D4(instruction_decoder_1_d4), .D5(instruction_decoder_1_d5), .D6(instruction_decoder_1_d6),
    .D7(instruction_decoder_1_d7), .D8(instruction_decoder_1_d8), .D9(instruction_decoder_1_d9),
    .D10(instruction_decoder_1_d10), .D11(instruction_decoder_1_d11), .D12(instruction_decoder_1_d12),
    .D13(instruction_decoder_1_d13), .D14(instruction_decoder_1_d14), .D15(instruction_decoder_1_d15), .E(E),
    .Z(Z), .T0(timing_decoder_1_t0), .T1(timing_decoder_1_t1), .T2(timing_decoder_1_t2),
    .T3(timing_decoder_1_t3), .T4(timing_decoder_1_t4), .T5(timing_decoder_1_t5), .T6(timing_decoder_1_t6),
    .T7(timing_decoder_1_t7), .T8(timing_decoder_1_t8), .T9(timing_decoder_1_t9), .T10(timing_decoder_1_t10),
    .T11(timing_decoder_1_t11), .T12(timing_decoder_1_t12), .T13(timing_decoder_1_t13),
    .T14(timing_decoder_1_t14), .T15(timing_decoder_1_t15), .AC_OUT(AC_OUT), .ADD(ADD), .ANDD(ANDD),
    .CMA(CMA), .CLA(CLA), .MEM_READ(MEM_READ), .MEM_WRITE(MEM_WRITE), .AR_OUT(AR_OUT), .AR_INC(AR_INC),
    .INPR_OUT(INPR_OUT), .OUTR_LD(OUTR_LD), .FGI_CLR(control_logic_1_fgi_clr),
    .FGO_CLR(control_logic_1_fgo_clr), .CLE(CLE), .S_CLR(control_logic_1_s_clr), .out_63(STOP),
    .SC_CLR(control_logic_1_sc_clr), .INPR_LD(INPR_LD), .AR_LD(AR_LD), .PC_out(PC_OUT), .PC_INC(PC_INC),
    .PC_LD(PC_LD), .IR_LD(IR_LD), .IR_ADDER_OUT(IR_ADDER_OUT), .DR_LD(DR_LD), .DR_INC(DR_INC),
    .DR_OUT(DR_OUT), .AC_LD(AC_LD));
  FLAGS_I_O flags_i_o_1 (
    .D_I(D_FGI), .D_O(1'b1), .R_I(control_logic_1_fgi_clr), .CLK(in_7), .R_O(control_logic_1_fgo_clr),
    .Q_I(flags_i_o_1_q_i), .Q_O(flags_i_o_1_q_o));
  Instruction_Decoder instruction_decoder_1 (
    .S(OPCODE), .D0(instruction_decoder_1_d0), .D15(instruction_decoder_1_d15),
    .D1(instruction_decoder_1_d1), .D14(instruction_decoder_1_d14), .D2(instruction_decoder_1_d2),
    .D13(instruction_decoder_1_d13), .D3(instruction_decoder_1_d3), .D12(instruction_decoder_1_d12),
    .D4(instruction_decoder_1_d4), .D11(instruction_decoder_1_d11), .D5(instruction_decoder_1_d5),
    .D10(instruction_decoder_1_d10), .D6(instruction_decoder_1_d6), .D9(instruction_decoder_1_d9),
    .D7(instruction_decoder_1_d7), .D8(instruction_decoder_1_d8));

  assign out_34 = RESET;
  assign out_35 = RESET;
  assign out_36 = RESET;
  assign out_37 = RESET;
  assign out_38 = RESET;
  assign out_39 = RESET;
  assign out_40 = RESET;

  // Other names for the same wires on the sheet: CLK = in_7

  // Notes on the sheet:
  //   CONTROLL UNIT
endmodule

module AR_REGISTER (
  input  [15:0] D_in,
  input  AR_OUT,
  input  RESET,
  input  LD,
  input  CLR,
  input  INC,
  input  CLK,
  output [10:0] Q,
  output [15:0] Q_Out,
  output out_10
);

  wire and_2_out, not_1_out, or_1_out, t_flip_flop_1_out_2;
  wire [0:0] and_1_out;
  wire [10:0] adder_1_out, multiplexer_1_out, register_1_q;

  or or_1 (or_1_out, LD, and_2_out, CLR);
  Register #(.width(11)) register_1 (.D(multiplexer_1_out), .en(or_1_out), .clk(CLK), .Q(register_1_q), .clr(RESET));
  Adder #(.width(11)) adder_1 (.a(register_1_q), .b(11'h1), .out(adder_1_out));  // open: cin, cout
  assign Q = register_1_q;  // Buffer buffer_1, 11 bits wide
  assign Q_Out = {{5{1'b0}}, register_1_q};  // Bit_Extender bit_extender_1
  Multiplexer #(.select(2), .width(11)) multiplexer_1 (
    .in0(D_in[10:0]), .in1(adder_1_out), .in2({11{1'b0}}), .out(multiplexer_1_out), .sel({CLR, and_1_out[0]}));  // open: in3
  and and_1 (and_1_out[0], not_1_out, and_2_out);
  not not_1 (not_1_out, CLR);
  and and_2 (and_2_out, INC, t_flip_flop_1_out_2);
  T_FLIP_FLOP t_flip_flop_1 (.CLK(CLK), .out_2(t_flip_flop_1_out_2));

  assign out_10 = AR_OUT;
endmodule

module PC_REGISTER (
  input  [15:0] D_in,
  input  PC_OUT,
  input  RESET,
  input  LD,
  input  CLR,
  input  INC,
  input  CLK,
  output [15:0] Q_Out,
  output out_9
);

  wire and_2_out, not_1_out, or_1_out, t_flip_flop_1_out_2;
  wire [0:0] and_1_out;
  wire [10:0] adder_1_out, multiplexer_1_out, register_1_q;

  or or_1 (or_1_out, LD, and_2_out, CLR);
  Register #(.width(11)) register_1 (.D(multiplexer_1_out), .en(or_1_out), .clk(CLK), .Q(register_1_q), .clr(RESET));
  Adder #(.width(11)) adder_1 (.a(register_1_q), .b(11'h1), .out(adder_1_out));  // open: cin, cout
  assign Q_Out = {{5{1'b0}}, register_1_q};  // Bit_Extender bit_extender_1
  Multiplexer #(.select(2), .width(11)) multiplexer_1 (
    .in0(D_in[10:0]), .in1(adder_1_out), .in2({11{1'b0}}), .out(multiplexer_1_out), .sel({CLR, and_1_out[0]}));  // open: in3
  and and_1 (and_1_out[0], not_1_out, and_2_out);
  not not_1 (not_1_out, CLR);
  and and_2 (and_2_out, INC, t_flip_flop_1_out_2);
  T_FLIP_FLOP t_flip_flop_1 (.CLK(CLK), .out_2(t_flip_flop_1_out_2));

  assign out_9 = PC_OUT;
endmodule

module IR_REGISTER (
  input  [15:0] D_in,
  input  LD,
  input  CLK,
  input  IR_ADDER_OUT,
  input  RESET,
  output [15:0] IR_ADDR,
  output IR_I,
  output [3:0] IR_OPCODE,
  output out_9
);

  wire [10:0] register_1_q;

  Register #(.width(16)) register_1 (.D(D_in), .en(LD), .clk(CLK), .Q({IR_OPCODE, IR_I, register_1_q}), .clr(RESET));
  assign IR_ADDR = {{5{register_1_q[10]}}, register_1_q};  // Bit_Extender bit_extender_1

  assign out_9 = IR_ADDER_OUT;
endmodule

module DR_REGISTER (
  input  [15:0] D_in,
  input  DR_OUT,
  input  CLK,
  input  RESET,
  input  CLR,
  input  INC,
  input  LD,
  output [15:0] Q,
  output [15:0] Q_OUT,
  output out_10
);

  wire not_1_out, or_1_out;
  wire [0:0] and_1_out;
  wire [15:0] adder_1_out, multiplexer_1_out;

  or or_1 (or_1_out, LD, INC, CLR);
  Register #(.width(16)) register_1 (.D(multiplexer_1_out), .en(or_1_out), .clk(CLK), .Q(Q_OUT), .clr(RESET));
  assign Q = Q_OUT;  // Buffer buffer_1, 16 bits wide
  Adder #(.width(16)) adder_1 (.a(Q_OUT), .b(16'h1), .out(adder_1_out));  // open: cin, cout
  Multiplexer #(.select(2), .width(16)) multiplexer_1 (
    .in0(D_in), .in1(adder_1_out), .in2({16{1'b0}}), .out(multiplexer_1_out), .sel({CLR, and_1_out[0]}));  // open: in3
  and and_1 (and_1_out[0], not_1_out, INC);
  not not_1 (not_1_out, CLR);

  assign out_10 = DR_OUT;
endmodule

module AC_REGISTER (
  input  [15:0] D_in,
  input  LD,
  input  CLK,
  input  AC_OUT,
  input  CLR,
  input  RESET,
  output [15:0] Q_OUT,
  output [15:0] Q,
  output out_9
);

  wire and_1_out, or_1_out, t_flip_flop_1_out_2;

  Register #(.width(16)) register_1 (.D(D_in), .en(and_1_out), .clk(CLK), .Q(Q_OUT), .clr(or_1_out));
  and and_1 (and_1_out, LD, t_flip_flop_1_out_2);
  T_FLIP_FLOP t_flip_flop_1 (.CLK(CLK), .out_2(t_flip_flop_1_out_2));
  or or_1 (or_1_out, CLR, RESET);
  assign Q = Q_OUT;  // Buffer buffer_1, 16 bits wide

  assign out_9 = AC_OUT;
endmodule

module INPR_REGISTER (
  input  [7:0] D_in,
  input  LD,
  input  CLK,
  input  RESET,
  input  AR_OUT,
  output [15:0] Q_Out,
  output out_7
);

  wire [7:0] register_1_q;

  Register register_1 (.D(D_in), .en(LD), .clk(CLK), .Q(register_1_q), .clr(RESET));
  assign Q_Out = {{8{1'b0}}, register_1_q};  // Bit_Extender bit_extender_1

  assign out_7 = AR_OUT;
endmodule

module OUTR_REGISTER (
  input  [15:0] D_in,
  input  LD,
  input  CLK,
  input  RESET,
  output [7:0] Q_Out
);

  Register register_1 (.D(D_in[7:0]), .en(LD), .clk(CLK), .Q(Q_Out), .clr(RESET));
endmodule

module ALU (
  input  [15:0] B,
  input  [15:0] A,
  input  [1:0] S,
  input  EN_MUX,
  output E,
  output Z,
  output [15:0] O,
  output out_8
);

  wire or_1_out;
  wire [15:0] adder_1_out, multiplier_1_out, not_1_out;

  Adder #(.width(16)) adder_1 (.a(A), .b(B), .out(adder_1_out), .cout(E));  // open: cin
  Multiplier #(.width(16)) multiplier_1 (.a(A), .b(B), .out(multiplier_1_out));  // open: cin, cout
  assign not_1_out = ~A;  // NOT_Gate not_1, 16 bits wide
  Multiplexer #(.select(2), .width(16)) multiplexer_1 (
    .in0(adder_1_out), .in1(multiplier_1_out), .in2(not_1_out), .in3({16{1'b0}}), .out(O), .sel(S));
  not not_2 (Z, or_1_out);
  or or_1 (or_1_out, O[0], O[1], O[2], O[3], O[4], O[5], O[6], O[7], O[8], O[9], O[10], O[11], O[12], O[13], O[14], O[15]);

  assign out_8 = EN_MUX;
endmodule

module DATA_BUS (
  input  [10:0] AR_Q,
  input  [15:0] DR_Q,
  input  [15:0] AC_Q,
  input  [15:0] in_4,
  input  [15:0] in_5,
  input  [15:0] in_6,
  input  [15:0] in_7,
  input  [15:0] in_8,
  input  [15:0] in_9,
  input  [15:0] in_10,
  input  [15:0] in_11,
  input  INPR_OUT,
  input  DR_OUT,
  input  MEM_READ,
  input  PC_OUT,
  input  IR_ADDER_OUT,
  input  AC_OUT,
  input  AR_OUT,
  input  ALU_OUT,
  output [10:0] MEM_A,
  output [15:0] B,
  output [15:0] A,
  output [15:0] out_23,
  output [15:0] out_24,
  output [15:0] out_25,
  output [15:0] out_26,
  output [15:0] out_27,
  output [15:0] out_28,
  output [15:0] out_29
);

  wire [2:0] priority_encoder_1_out;

  Priority_Encoder priority_encoder_1 (
    .in0(INPR_OUT), .in1(DR_OUT), .in2(MEM_READ), .in3(PC_OUT), .in4(IR_ADDER_OUT), .in5(AC_OUT),
    .in6(AR_OUT), .in7(ALU_OUT), .out(priority_encoder_1_out));  // open: en_in
  Multiplexer #(.select(3), .width(16)) multiplexer_1 (
    .in0(in_4), .in1(in_5), .in2(in_6), .in3(in_7), .in4(in_8), .in5(in_9), .in6(in_10), .in7(in_11),
    .out(out_23), .sel(priority_encoder_1_out));

  assign A = AC_Q;
  assign B = DR_Q;
  assign MEM_A = AR_Q;
  assign out_24 = out_23;
  assign out_25 = out_23;
  assign out_26 = out_23;
  assign out_27 = out_23;
  assign out_28 = out_23;
  assign out_29 = out_23;

  // Notes on the sheet:
  //   DATA BUS
endmodule

module FLAGS (
  input  E,
  input  in_2,
  input  Z,
  input  in_4,
  input  CLK,
  output out_6,
  output out_7
);

  D_Flip_Flop d_ff_1 (.D(E), .clk(CLK), .Q(out_6), .reset(in_2));  // open: Qn, preset
  D_Flip_Flop d_ff_2 (.D(Z), .clk(CLK), .Q(out_7), .reset(in_4));  // open: Qn, preset
endmodule

module MEMORY (
  input  WE,
  input  [10:0] A,
  input  O_E,
  input  CLK,
  input  [15:0] D,
  output out_6,
  output [15:0] Q
);

  RAM #(.addrWidth(10), .dataWidth(16)) ram_1 (.addr(A[9:0]), .we(WE), .oe(O_E), .clk(CLK), .din(D), .dout(Q));

  assign out_6 = O_E;
endmodule

module SELECT_ALU (
  input  ADD,
  input  ANDD,
  input  CMA,
  input  CLA,
  output EN,
  output [1:0] S
);

  wire [0:0] not_4_out;
  wire [1:0] not_1_out;
  wire [1:1] not_3_out;

  NotExactlyOne xnor_1[1:0] (
    .out(S), .in0(not_1_out), .in1({not_3_out[1], ANDD}), .in2({CMA, not_4_out[0]}), .in3({2{CLA}}));
  or or_1 (EN, ADD, ANDD, CMA, CLA);
  not not_1 (not_1_out[0], ADD);
  not not_2 (not_1_out[1], ADD);
  not not_3 (not_3_out[1], ANDD);
  not not_4 (not_4_out[0], CMA);
endmodule

module Sequence_Counter (
  input  RESET,
  input  EN_INC,
  input  CLK,
  output [3:0] O_P
);

  wire and_1_out, t_flip_flop_1_out_2;

  T_FLIP_FLOP t_flip_flop_1 (.CLK(CLK), .out_2(t_flip_flop_1_out_2));
  Counter #(.max('hf), .width(4)) counter_1 (
    .clr(and_1_out), .load(1'b0), .up(1'b1), .count(EN_INC), .clk(CLK), .Q(O_P));  // open: D, carry
  and and_1 (and_1_out, t_flip_flop_1_out_2, RESET);
endmodule

module Timing_Decoder (
  input  [3:0] SC,
  output T0,
  output T1,
  output T2,
  output T3,
  output T4,
  output T5,
  output T6,
  output T7,
  output T15,
  output T14,
  output T13,
  output T12,
  output T11,
  output T10,
  output T9,
  output T8
);

  Decoder #(.enable("false"), .select(4)) decoder_1 (
    .out0(T0), .out1(T1), .out2(T2), .out3(T3), .out4(T4), .out5(T5), .out6(T6), .out7(T7), .out8(T8),
    .out9(T9), .out10(T10), .out11(T11), .out12(T12), .out13(T13), .out14(T14), .out15(T15), .sel(SC));
endmodule

module Instruction_Decoder (
  input  [3:0] S,
  output D0,
  output D1,
  output D2,
  output D3,
  output D4,
  output D5,
  output D6,
  output D7,
  output D15,
  output D14,
  output D13,
  output D12,
  output D11,
  output D10,
  output D9,
  output D8
);

  Decoder #(.enable("false"), .select(4)) decoder_1 (
    .out0(D0), .out1(D1), .out2(D2), .out3(D3), .out4(D4), .out5(D5), .out6(D6), .out7(D7), .out8(D8),
    .out9(D9), .out10(D10), .out11(D11), .out12(D12), .out13(D13), .out14(D14), .out15(D15), .sel(S));
endmodule

module Control_Logic (
  input  IR_I,
  input  E,
  input  FGO,
  input  Z,
  input  FGI,
  input  T0,
  input  D0,
  input  T1,
  input  D1,
  input  T2,
  input  D2,
  input  T3,
  input  D3,
  input  T4,
  input  D4,
  input  T5,
  input  D5,
  input  T6,
  input  D6,
  input  T7,
  input  D7,
  input  T8,
  input  D8,
  input  T9,
  input  D9,
  input  T10,
  input  D10,
  input  T11,
  input  D11,
  input  T12,
  input  D12,
  input  T13,
  input  D13,
  input  T14,
  input  D14,
  input  T15,
  input  D15,
  output AR_LD,
  output PC_out,
  output PC_INC,
  output PC_LD,
  output IR_LD,
  output IR_ADDER_OUT,
  output DR_LD,
  output DR_INC,
  output DR_OUT,
  output AC_LD,
  output AC_OUT,
  output ADD,
  output ANDD,
  output CMA,
  output CLA,
  output MEM_READ,
  output MEM_WRITE,
  output AR_OUT,
  output AR_INC,
  output INPR_OUT,
  output OUTR_LD,
  output FGI_CLR,
  output FGO_CLR,
  output CLE,
  output S_CLR,
  output out_63,
  output SC_CLR,
  output INPR_LD
);

  wire and_1_out, and_2_out, and_3_out, and_4_out, and_5_out, and_6_out, and_7_out, and_8_out, and_9_out,
       and_10_out, and_12_out, and_13_out, and_14_out, and_15_out, and_16_out, and_17_out, and_18_out,
       and_19_out, and_20_out, and_21_out, and_22_out, and_27_out, and_28_out, and_29_out, and_30_out,
       and_31_out, and_32_out, and_33_out, and_34_out, and_35_out, and_43_out, and_44_out, and_45_out,
       and_46_out, and_47_out, and_48_out, and_49_out, and_50_out, and_51_out, and_52_out, and_53_out,
       and_54_out, and_55_out, and_56_out, and_57_out, or_12_out;

  or or_1 (AR_LD, T0, T2);
  and and_1 (and_1_out, T3, D9);
  and and_2 (and_2_out, T5, Z, D7);
  or or_2 (PC_out, and_1_out, T0);
  and and_3 (and_3_out, FGO, D14, T3);
  and and_4 (and_4_out, FGI, D13, T3);
  and and_5 (and_5_out, D8, T3);
  or or_3 (PC_INC, and_2_out, and_3_out, and_4_out, T1);
  and and_6 (and_6_out, D9, T5);
  or or_4 (PC_LD, and_5_out, and_6_out);
  and and_7 (and_7_out, T3, D0);
  and and_8 (and_8_out, T3, D3);
  and and_9 (and_9_out, T3, D4);
  or or_5 (DR_LD, and_7_out, and_8_out, and_9_out, and_10_out);
  and and_10 (and_10_out, T3, D7);
  and and_11 (DR_INC, T4, D7);
  and and_12 (and_12_out, D0, T4);
  and and_13 (and_13_out, D7, T5);
  and and_14 (and_14_out, D0, T4);
  or or_6 (DR_OUT, and_12_out, and_13_out);
  and and_15 (and_15_out, D3, T4);
  and and_16 (and_16_out, D4, T4);
  and and_17 (and_17_out, D5, T3);
  or or_7 (AC_LD, and_14_out, and_15_out, and_16_out, and_17_out, and_20_out, and_18_out);
  and and_18 (and_18_out, D11, T3);
  and and_19 (and_19_out, D1, T3);
  and and_20 (and_20_out, D6, T3);
  and and_21 (and_21_out, T9, T3);
  and and_22 (and_22_out, D12, T3);
  or or_8 (AC_OUT, and_19_out, and_21_out, and_22_out);
  and and_23 (ADD, D3, T4);
  and and_24 (ANDD, D4, T4);
  and and_25 (CMA, D5, T3);
  and and_26 (CLA, D6, T3);
  and and_27 (and_27_out, D0, T3);
  and and_28 (and_28_out, D3, T3);
  and and_29 (and_29_out, D4, T3);
  and and_30 (and_30_out, D7, T3);
  or or_9 (MEM_READ, and_27_out, and_28_out, and_29_out, and_30_out, T1);
  and and_31 (and_31_out, D1, T3);
  and and_32 (and_32_out, D7, T5);
  and and_33 (and_33_out, D9, T3);
  or or_10 (MEM_WRITE, and_31_out, and_32_out, and_33_out);
  and and_34 (and_34_out, D8, T3);
  and and_35 (and_35_out, D9, T5);
  or or_11 (AR_OUT, and_34_out, and_35_out);
  and and_36 (AR_INC, T4, D9);
  and and_37 (INPR_OUT, T3, D11);
  and and_38 (OUTR_LD, T3, D12);
  and and_39 (FGI_CLR, D11, T3);
  and and_40 (FGO_CLR, D12, T5);
  and and_41 (CLE, T3, D10);
  or or_12 (or_12_out, T5, T0);
  and and_42 (out_63, D15, or_12_out);
  and and_43 (and_43_out, D0, T5);
  and and_44 (and_44_out, D1, T5);
  and and_45 (and_45_out, D3, T5);
  and and_46 (and_46_out, D4, T5);
  and and_47 (and_47_out, D5, T5);
  and and_48 (and_48_out, D6, T5);
  and and_49 (and_49_out, D7, T5);
  and and_50 (and_50_out, D8, T4);
  or or_13 (SC_CLR, and_43_out, and_44_out, and_45_out, and_46_out, and_47_out, and_48_out, and_49_out, and_50_out, and_51_out, and_52_out, and_53_out, and_54_out, and_55_out, and_56_out, and_57_out);
  and and_51 (and_51_out, D9, T5);
  and and_52 (and_52_out, D10, T5);
  and and_53 (and_53_out, D11, T5);
  and and_54 (and_54_out, D12, T5);
  and and_55 (and_55_out, D13, T5);
  and and_56 (and_56_out, D14, T5);
  and and_57 (and_57_out, D15, T5);

  assign INPR_LD = FGI;
  assign IR_ADDER_OUT = T2;
  assign IR_LD = T1;
  assign S_CLR = out_63;

  // Notes on the sheet:
  //   CONTROLL LOGIC
endmodule

module FLAGS_I_O (
  input  D_I,
  input  CLK,
  input  D_O,
  input  R_I,
  input  R_O,
  output Q_I,
  output Q_O
);

  wire or_1_out, or_2_out;

  or or_1 (or_1_out, Q_I, D_I);
  or or_2 (or_2_out, D_O, Q_O);
  D_Flip_Flop d_ff_1 (.D(or_1_out), .clk(CLK), .Q(Q_I), .reset(R_I));  // open: Qn, preset
  D_Flip_Flop d_ff_2 (.D(or_2_out), .clk(CLK), .Q(Q_O), .reset(R_O));  // open: Qn, preset
endmodule

module S_FLAG (
  input  START,
  input  CLK,
  input  RESET,
  output OUT_PUT
);

  wire and_1_out, not_1_out, or_1_out;

  not not_1 (not_1_out, OUT_PUT);
  and and_1 (and_1_out, not_1_out, START);
  or or_1 (or_1_out, and_1_out, OUT_PUT);
  D_Flip_Flop d_ff_1 (.D(or_1_out), .clk(CLK), .Q(OUT_PUT), .reset(RESET));  // open: Qn, preset
endmodule

module T_FLIP_FLOP (
  input  CLK,
  output out_2
);

  T_Flip_Flop #(.trigger("falling")) t_ff_1 (.T(1'b1), .clk(CLK), .Q(out_2));  // open: Qn, reset, preset
endmodule

module T_FLIP_RISING (
  input  CLK,
  output out_2
);

  T_Flip_Flop t_ff_1 (.T(1'b1), .clk(CLK), .Q(out_2));  // open: Qn, reset, preset
endmodule

module B_TO_D (
  input  [7:0] in_1,
  output [3:0] out_2,
  output [3:0] out_3,
  output [3:0] out_4
);

  // Binary_to_BCD_converter #(.binvalue(8)) binary_to_bcd_converter_1: pin names not known; wires that end beside it: in_1, out_2, out_3, out_4
endmodule

module INPUTS (
  input  [7:0] in_1,
  input  in_2,
  input  in_3,
  input  in_4,
  input  in_5,
  input  in_6,
  input  in_7,
  input  in_8,
  input  in_9,
  output [7:0] out_10
);

  assign out_10 = {in_2, in_3, in_4, in_5, in_6, in_7, in_8, in_9} | in_1;  // OR_Gate or_1, 8 bits wide
endmodule

module OUTPUTS (
  input  [7:0] in_1,
  output out_2,
  output out_3,
  output out_4,
  output out_5,
  output out_6,
  output out_7,
  output out_8,
  output out_9,
  output [7:0] out_10
);


  assign out_2 = in_1[7];
  assign out_3 = in_1[6];
  assign out_4 = in_1[5];
  assign out_5 = in_1[4];
  assign out_6 = in_1[3];
  assign out_7 = in_1[2];
  assign out_8 = in_1[1];
  assign out_9 = in_1[0];
  assign out_10 = in_1;
endmodule
